# Fritzing sketch basic-robot (saved by Fritzing 0.9.1b)
circuit board: 5.44256cm x 4.96438cm
breadboards: 1

parts:
  MCU = Arduino Nano (Rev3.0)
  Bat1 = 4 x AAA Battery Mount
  Bat2 = Battery
  S1 = Toggle Switch [package=THT]
  Right_Servo = Basic Servo
  Left_Servo = Basic Servo
  R1 = Photocell (LDR) [package=THT]
  R2 = Resistor [tolerance=±5% resistance=10k package=THT]
  R3 = Resistor [tolerance=±5% resistance=100 package=THT]
  LED1 = LED - 5mm [color="Red (633nm)" package="5 mm [THT]"]
  LED2 = LED - 5mm [color="Infrared (940nm)" package="5 mm [THT]"]
  R4 = Resistor [tolerance=±5% resistance=100 package=THT]
  S2 = Pushbutton [package=THT]
  R5 = Resistor [tolerance=±5% resistance=10k package=THT]
  IR-Right = mystery part, 3 pins [chip_label=IR]
  IR-Left = mystery part, 3 pins [chip_label=IR]

nets:
  GND: MCU.GND, Bat2.-, Right_Servo.gnd, Left_Servo.gnd, R2.Pin_1, R3.Pin_1, LED2.cathode, R5.Pin_1, IR-Right.pin2, IR-Left.pin2
  N1: MCU.D2, IR-Left.pin1
  N2: MCU.D3, R4.Pin_0
  N3: MCU.D4, IR-Right.pin1
  N4: MCU.D7, S2.leg0, R5.Pin_0
  N5: MCU.D9, Left_Servo.pulse
  N6: MCU.D10, Right_Servo.pulse
  Vbat: MCU.VIN, S1.COM, Right_Servo.vcc, Left_Servo.vcc
  5V: MCU.5V, R1.pin_0, LED1.anode, S2.leg1, IR-Right.pin3, IR-Left.pin3
  N7: MCU.A0, R1.pin_1, R2.Pin_0
  N8: Bat1.-, Bat2.+
  N9: Bat1.+, S1.L1
  N10: R3.Pin_0, LED1.cathode
  N11: LED2.anode, R4.Pin_1
