# Fritzing sketch sumo-robot (saved by Fritzing 0.9.1b)
breadboards: 1

parts:
  MCU = Arduino Nano (Rev3.0)
  Bat1 = Battery block 9V
  Bat2-4x-AA = 4 x AAA Battery Mount [part_number=4.8V]
  R1 = Photocell (LDR) [package=THT]
  R2 = Resistor [tolerance=±5% resistance=10k package=THT]
  LED1 = LED - 5mm [color="Red (633nm)" package="5 mm [THT]"]
  R3 = Resistor [tolerance=±5% resistance=330 package=THT]
  S1 = SWITCH-DPDT [package=gpi-152-3013]
  Right_Servo = Basic Servo
  Lrft_Servo = Basic Servo
  IR_Left = mystery part, 3 pins [chip_label=IR]
  IR_Right = mystery part, 3 pins [chip_label=IR]
  R4 = Resistor [tolerance=±5% resistance=100 package=THT]
  LED2 = LED - 5mm [color="Infrared (940nm)" package="5 mm [THT]"]
  LED3 = LED - 5mm [color="Infrared (940nm)" package="5 mm [THT]"]

nets:
  GND: MCU.GND, Bat1.-, Bat2-4x-AA.-, R2.Pin_1, R3.Pin_1, Right_Servo.gnd, Lrft_Servo.gnd, IR_Left.pin2, IR_Right.pin2, LED3.cathode
  N1: MCU.D2, IR_Left.pin1
  N2: MCU.D3, R4.Pin_0
  N3: MCU.D4, IR_Right.pin1
  N4: MCU.D9, Lrft_Servo.pulse
  N5: MCU.D10, Right_Servo.pulse
  N6: MCU.VIN, S1.2
  5V: MCU.5V, R1.pin_0, LED1.anode, IR_Left.pin3, IR_Right.pin3
  N7: MCU.A0, R1.pin_1, R2.Pin_0
  N8: Bat1.+, S1.3
  N9: Bat2-4x-AA.+, S1.6
  N10: LED1.cathode, R3.Pin_0
  VCC: S1.5, Right_Servo.vcc, Lrft_Servo.vcc
  N11: R4.Pin_1, LED2.anode
  N12: LED2.cathode, LED3.anode
